// Logisim project braile.circ as structural Verilog: 4 circuits, main circuit main
module main (
  input  b1,
  input  b2,
  input  b3,
  input  b4,
  input  in_5,
  input  in_6,
  input  in_7,
  input  in_8,
  output out_9,
  output out_10,
  output out_11,
  output out_12,
  output out_13,
  output out_14,
  output out_15,
  output out_16,
  output out_17,
  output out_18,
  output out_19,
  output out_20
);

  wire \decodificador_de_padrões_1_out_5 , \decodificador_de_padrões_1_out_6 ,
       \decodificador_de_padrões_1_out_7 , levantador_de_pinos_de_prefixo_1_out_8;

  \decodificador_de_padrões  \decodificador_de_padrões_1  (
    .b1(b1), .b2(b2), .b3(b3), .b4(b4), .out_5(\decodificador_de_padrões_1_out_5 ),
    .out_6(\decodificador_de_padrões_1_out_6 ), .out_7(\decodificador_de_padrões_1_out_7 ));
  levantador_de_pinos_de_prefixo levantador_de_pinos_de_prefixo_1 (
    .in_1(\decodificador_de_padrões_1_out_7 ), .in_2(\decodificador_de_padrões_1_out_6 ),
    .in_3(\decodificador_de_padrões_1_out_5 ), .out_4(out_10), .out_5(out_18), .out_6(out_17),
    .out_7(out_14), .out_8(levantador_de_pinos_de_prefixo_1_out_8));
  LED led_1 (.in(levantador_de_pinos_de_prefixo_1_out_8));

  // Notes on the sheet:
  //   lógica para prefixos
  //   levantador de pinos de prefixo
  //   pinos
  //   4
  //   6
  //   3
  //   5
endmodule

module \decodificador_de_padrões  (
  input  b1,
  input  b2,
  input  b3,
  input  b4,
  output out_5,
  output out_6,
  output out_7
);

  wire and_1_out, and_2_out, and_3_out, and_4_out, and_5_out, and_6_out, and_8_out, and_9_out, and_10_out,
       not_1_out, not_2_out, not_3_out, not_4_out, not_5_out, not_6_out, not_7_out, not_8_out, not_9_out,
       not_10_out, not_11_out, not_12_out, not_13_out, not_14_out, not_15_out, not_16_out, not_17_out,
       or_1_out, or_2_out, or_3_out, or_4_out, or_5_out;

  not not_1 (not_1_out, b1);
  not not_2 (not_2_out, b3);
  not not_3 (not_3_out, b4);
  not not_4 (not_4_out, b1);
  not not_5 (not_5_out, b3);
  not not_6 (not_6_out, b2);
  not not_7 (not_7_out, b3);
  not not_8 (not_8_out, b2);
  not not_9 (not_9_out, b3);
  not not_10 (not_10_out, b4);
  not not_11 (not_11_out, b1);
  not not_12 (not_12_out, b2);
  not not_13 (not_13_out, b2);
  not not_14 (not_14_out, b4);
  not not_15 (not_15_out, b1);
  not not_16 (not_16_out, b4);
  not not_17 (not_17_out, b1);
  and and_1 (and_1_out, not_1_out, b2, not_2_out, not_3_out);
  and and_2 (and_2_out, not_4_out, b2, not_5_out, b4);
  and and_3 (and_3_out, b1, not_6_out, not_7_out, b4);
  and and_4 (and_4_out, b1, not_8_out, b3, b4);
  and and_5 (and_5_out, b1, b2, not_9_out, b4);
  and and_6 (and_6_out, b1, b2, b3, not_10_out);
  and and_7 (out_6, not_11_out, not_12_out, b3, b4);
  and and_8 (and_8_out, b1, not_13_out, b3, not_14_out);
  and and_9 (and_9_out, not_15_out, b2, b3, not_16_out);
  and and_10 (and_10_out, not_17_out, b2, b3, b4);
  or or_1 (or_1_out, and_1_out, and_2_out);
  or or_2 (or_2_out, and_3_out, and_4_out);
  or or_3 (or_3_out, and_5_out, and_6_out);
  or or_4 (or_4_out, and_8_out, and_9_out);
  or or_5 (or_5_out, or_1_out, or_2_out);
  or or_6 (out_5, or_5_out, or_3_out);
  or or_7 (out_7, or_4_out, and_10_out);

  // Notes on the sheet:
  //   Entradas fora do sub
  //   0100 | A - O MAIUSCULO
  //   0101 | P+ MAIUSCULO
  //   1001| É MAIUSCULO
  //   1011| Â À Á MAIUSCULO
  //   1101| Ê Í MAIUSCULO
  //   1110| Ó Ô Ú MAIUSCULO
  //   0011 | 0 - 9
  //   1010 | á í ó ú MINUSCULO
  //   0110 | a - o MINUSCULO
  //   0111 | p+ MINUSCULO
endmodule

module levantador_de_pinos_de_prefixo (
  input  in_1,
  input  in_2,
  input  in_3,
  output out_4,
  output out_5,
  output out_6,
  output out_7,
  output out_8
);

  wire and_1_out, not_1_out, not_2_out, not_3_out, not_4_out, not_5_out, not_6_out, not_7_out;

  not not_1 (not_1_out, in_2);
  not not_2 (not_2_out, in_1);
  not not_3 (not_3_out, in_3);
  not not_4 (not_4_out, in_1);
  not not_5 (not_5_out, in_3);
  not not_6 (not_6_out, in_2);
  and and_1 (and_1_out, in_3, not_1_out, not_2_out);
  and and_2 (out_6, not_3_out, in_2, not_4_out);
  and and_3 (out_8, not_5_out, not_6_out, in_1);
  not not_7 (not_7_out, out_6);
  xnor xnor_1 (out_4, and_1_out, not_7_out);

  assign out_5 = out_4;
  assign out_7 = out_6;

  // Notes on the sheet:
  //   MAIUSCULAS | 46 (M1)
  //   NUMEROS | 3456 (M1)
  //   MINUSCULOS | NENHUM (M1)
endmodule

module decodificador_de_padroes_de_letras (
  input  in_1,
  input  in_2,
  input  in_3,
  input  in_4
);
endmodule
